// Logisim project problem1.circ as structural Verilog: 1 circuit, main circuit main
module main (
);

  wire d_ff_1_q, d_ff_2_q, d_ff_3_q, d_ff_4_q, d_ff_5_q, d_ff_6_q, multiplexer_1_out, multiplexer_2_out,
       multiplexer_3_out, undriven, undriven_2, undriven_3, undriven_4, undriven_5, undriven_6, undriven_7,
       undriven_8;

  D_Flip_Flop d_ff_1 (.clk(undriven_7), .D(undriven), .Q(d_ff_1_q));  // open: Qn, preset, en, reset
  D_Flip_Flop d_ff_2 (.clk(undriven_7), .D(undriven_2), .Q(d_ff_2_q));  // open: Qn, preset, en, reset
  D_Flip_Flop d_ff_3 (.clk(undriven_7), .D(undriven_3), .Q(d_ff_3_q));  // open: Qn, preset, en, reset
  D_Flip_Flop d_ff_4 (.clk(undriven_7), .D(undriven_4), .Q(d_ff_4_q));  // open: Qn, preset, en, reset
  D_Flip_Flop d_ff_5 (.clk(undriven_7), .D(undriven_5), .Q(d_ff_5_q));  // open: Qn, preset, en, reset
  D_Flip_Flop d_ff_6 (.clk(undriven_7), .D(undriven_6), .Q(d_ff_6_q));  // open: Qn, preset, en, reset
  Multiplexer #(.disabled(0), .enable("false")) multiplexer_1 (
    .in0(d_ff_1_q), .in1(d_ff_4_q), .out(multiplexer_1_out), .sel(undriven_8));
  Multiplexer #(.enable("false")) multiplexer_2 (
    .in0(d_ff_2_q), .in1(d_ff_5_q), .out(multiplexer_2_out), .sel(undriven_8));
  Multiplexer #(.enable("false")) multiplexer_3 (
    .in0(d_ff_3_q), .in1(d_ff_6_q), .out(multiplexer_3_out), .sel(undriven_8));

  // Notes on the sheet:
  //   register 0, bit 0
  //   register 0, bit 1
  //   register 0, bit 2
  //   register 1, bit 0
  //   register 1, bit 1
  //   register 1, bit 2
  //   clk
  //   register number
  //   read bit 0
  //   read bit 1
  //   read bit 2
endmodule
