// Logisim project problem1.circ as structural Verilog
module main (
);

  wire adder_1_cout, adder_1_out, and_1_out, multiplexer_1_out, multiplexer_2_out, multiplexer_3_out,
       not_1_out, not_2_out, or_1_out, undriven, undriven_2, undriven_3, undriven_4, undriven_5, undriven_6,
       undriven_7, xor_1_out;
  wire [1:0] undriven_8;

  not not_1 (not_1_out, undriven_2);
  not not_2 (not_2_out, undriven_4);
  Multiplexer #(.enable("false")) multiplexer_1 (
    .in0(undriven_2), .in1(not_1_out), .out(multiplexer_1_out), .sel(undriven));
  Multiplexer #(.enable("false")) multiplexer_2 (
    .in0(undriven_4), .in1(not_2_out), .out(multiplexer_2_out), .sel(undriven_3));
  Overflow_Detection overflow_detection_1 ();
  and and_1 (and_1_out, multiplexer_1_out, multiplexer_2_out);
  or or_1 (or_1_out, multiplexer_1_out, multiplexer_2_out);
  Adder #(.width(1)) adder_1 (
    .a(multiplexer_1_out), .b(multiplexer_2_out), .out(adder_1_out), .cin(undriven_6), .cout(adder_1_cout));
  Multiplexer #(.select(2), .enable("false")) multiplexer_3 (
    .in0(and_1_out), .in1(or_1_out), .in2(adder_1_out), .in3(undriven_5), .out(multiplexer_3_out),
    .sel(undriven_8));
  xor xor_1 (xor_1_out, adder_1_out, undriven_7);

  // Notes on the sheet:
  //   Ainvert
  //   a
  //   Binvert
  //   b
  //   less
  //   overflow detection
  //   carry in
  //   operation
  //   result
  //   set
  //   overflow
endmodule
