// Logisim project problem3.circ as structural Verilog: 2 circuits, main circuit main
module main (
);

  wire and_1_out, and_2_out, and_3_out, and_4_out, and_5_out, and_6_out, and_7_out, and_8_out, and_9_out,
       and_10_out, and_11_out, and_12_out, and_13_out, and_14_out, and_15_out, and_16_out, and_17_out,
       and_18_out, and_19_out, and_20_out, and_21_out, and_22_out, d_ff_1_q, d_ff_2_q, d_ff_3_q, d_ff_4_q,
       nor_1_out, not_1_out, not_2_out, not_3_out, not_4_out, not_5_out, not_6_out, not_7_out, not_8_out,
       not_9_out, not_10_out, not_11_out, not_12_out, not_13_out, not_14_out, or_1_out, or_2_out, or_3_out,
       or_4_out, or_5_out, or_6_out, or_7_out, or_8_out, S_0_q, S_1_q, undriven, undriven_2, undriven_3,
       undriven_4, undriven_5;

  nor nor_1 (nor_1_out, or_8_out, or_5_out, or_6_out, or_7_out);
  or or_1 (or_1_out, or_5_out, or_7_out);
  and and_1 (and_1_out, nor_1_out, S_0_q);
  or or_2 (or_2_out, or_6_out, or_7_out);
  and and_2 (and_2_out, nor_1_out, S_1_q);
  D_Flip_Flop d_ff_1 (.clk(undriven_5), .D(undriven), .Q(d_ff_1_q));  // open: Qn, preset, en, reset
  D_Flip_Flop d_ff_2 (.clk(undriven_5), .D(undriven_2), .Q(d_ff_2_q));  // open: Qn, preset, en, reset
  D_Flip_Flop d_ff_3 (.clk(undriven_5), .D(undriven_3), .Q(d_ff_3_q));  // open: Qn, preset, en, reset
  D_Flip_Flop d_ff_4 (.clk(undriven_5), .D(undriven_4), .Q(d_ff_4_q));  // open: Qn, preset, en, reset
  or or_3 (or_3_out, or_1_out, and_1_out);
  or or_4 (or_4_out, or_2_out, and_2_out);
  D_Flip_Flop S_0 (.clk(undriven_5), .D(or_3_out), .Q(S_0_q));  // open: Qn, preset, en, reset
  not not_1 (not_1_out, S_0_q);
  D_Flip_Flop S_1 (.clk(undriven_5), .D(or_4_out), .Q(S_1_q));  // open: Qn, preset, en, reset
  not not_2 (not_2_out, S_1_q);
  and and_3 (and_3_out, not_1_out, not_2_out);
  and and_4 (and_4_out, S_0_q, not_2_out);
  and and_5 (and_5_out, not_1_out, S_1_q);
  and and_6 (and_6_out, S_0_q, S_1_q);
  not not_3 (not_3_out, d_ff_1_q);
  not not_4 (not_4_out, d_ff_2_q);
  not not_5 (not_5_out, d_ff_3_q);
  not not_6 (not_6_out, d_ff_2_q);
  not not_7 (not_7_out, d_ff_3_q);
  not not_8 (not_8_out, d_ff_4_q);
  not not_9 (not_9_out, d_ff_3_q);
  not not_10 (not_10_out, d_ff_4_q);
  not not_11 (not_11_out, d_ff_1_q);
  not not_12 (not_12_out, d_ff_4_q);
  not not_13 (not_13_out, d_ff_1_q);
  not not_14 (not_14_out, d_ff_2_q);
  and and_7 (and_7_out, d_ff_1_q, and_3_out);
  and and_8 (and_8_out, not_3_out, d_ff_2_q, and_3_out);
  and and_9 (and_9_out, not_3_out, not_4_out, d_ff_3_q, and_3_out);
  and and_10 (and_10_out, not_3_out, not_4_out, not_5_out, d_ff_4_q, and_3_out);
  and and_11 (and_11_out, d_ff_2_q, and_4_out);
  and and_12 (and_12_out, not_6_out, d_ff_3_q, and_4_out);
  and and_13 (and_13_out, not_6_out, not_7_out, d_ff_4_q, and_4_out);
  and and_14 (and_14_out, not_6_out, not_7_out, not_8_out, d_ff_1_q, and_4_out);
  and and_15 (and_15_out, d_ff_3_q, and_5_out);
  and and_16 (and_16_out, not_9_out, d_ff_4_q, and_5_out);
  and and_17 (and_17_out, not_9_out, not_10_out, d_ff_1_q, and_5_out);
  and and_18 (and_18_out, not_9_out, not_10_out, not_11_out, d_ff_2_q, and_5_out);
  and and_19 (and_19_out, d_ff_4_q, and_6_out);
  and and_20 (and_20_out, not_12_out, d_ff_1_q, and_6_out);
  and and_21 (and_21_out, not_12_out, not_13_out, d_ff_2_q, and_6_out);
  and and_22 (and_22_out, not_12_out, not_13_out, not_14_out, d_ff_3_q, and_6_out);
  or or_5 (or_5_out, and_7_out, and_14_out, and_17_out, and_20_out);
  or or_6 (or_6_out, and_8_out, and_11_out, and_18_out, and_21_out);
  or or_7 (or_7_out, and_9_out, and_12_out, and_15_out, and_22_out);
  or or_8 (or_8_out, and_10_out, and_13_out, and_16_out, and_19_out);

  // Notes on the sheet:
  //   Clock
  //   Request_0
  //   Request_1
  //   Request_2
  //   Request_3
  //   Grant_0
  //   Grant_1
  //   Grant_2
  //   Grant_3
endmodule

module Test (
  input  Request_0,
  input  Request_1,
  input  Request_2,
  input  Request_3,
  output Grant_0,
  output Grant_1,
  output Grant_2,
  output Grant_3
);

  wire and_1_out, and_2_out, and_3_out, and_4_out, and_5_out, and_6_out, and_7_out, and_8_out, and_9_out,
       and_10_out, and_11_out, and_12_out, and_13_out, and_14_out, and_15_out, and_16_out, and_17_out,
       and_18_out, and_19_out, and_20_out, and_21_out, and_22_out, clock_1_out, d_ff_1_q, d_ff_2_q, d_ff_3_q,
       d_ff_4_q, nor_1_out, not_1_out, not_2_out, not_3_out, not_4_out, not_5_out, not_6_out, not_7_out,
       not_8_out, not_9_out, not_10_out, not_11_out, not_12_out, not_13_out, not_14_out, or_1_out, or_2_out,
       or_3_out, or_4_out, S_0_q, S_1_q;

  Clock clock_1 (.out(clock_1_out));
  nor nor_1 (nor_1_out, Grant_3, Grant_0, Grant_1, Grant_2);
  or or_1 (or_1_out, Grant_0, Grant_2);
  and and_1 (and_1_out, nor_1_out, S_0_q);
  or or_2 (or_2_out, Grant_1, Grant_2);
  and and_2 (and_2_out, nor_1_out, S_1_q);
  D_Flip_Flop d_ff_1 (.clk(clock_1_out), .D(Request_0), .Q(d_ff_1_q));  // open: Qn, preset, en, reset
  D_Flip_Flop d_ff_2 (.clk(clock_1_out), .D(Request_1), .Q(d_ff_2_q));  // open: Qn, preset, en, reset
  D_Flip_Flop d_ff_3 (.clk(clock_1_out), .D(Request_2), .Q(d_ff_3_q));  // open: Qn, preset, en, reset
  D_Flip_Flop d_ff_4 (.clk(clock_1_out), .D(Request_3), .Q(d_ff_4_q));  // open: Qn, preset, en, reset
  or or_3 (or_3_out, or_1_out, and_1_out);
  or or_4 (or_4_out, or_2_out, and_2_out);
  D_Flip_Flop S_0 (.clk(clock_1_out), .D(or_3_out), .Q(S_0_q));  // open: Qn, preset, en, reset
  not not_1 (not_1_out, S_0_q);
  D_Flip_Flop S_1 (.clk(clock_1_out), .D(or_4_out), .Q(S_1_q));  // open: Qn, preset, en, reset
  not not_2 (not_2_out, S_1_q);
  and and_3 (and_3_out, not_1_out, not_2_out);
  and and_4 (and_4_out, S_0_q, not_2_out);
  and and_5 (and_5_out, not_1_out, S_1_q);
  and and_6 (and_6_out, S_0_q, S_1_q);
  not not_3 (not_3_out, d_ff_1_q);
  not not_4 (not_4_out, d_ff_2_q);
  not not_5 (not_5_out, d_ff_3_q);
  not not_6 (not_6_out, d_ff_2_q);
  not not_7 (not_7_out, d_ff_3_q);
  not not_8 (not_8_out, d_ff_4_q);
  not not_9 (not_9_out, d_ff_3_q);
  not not_10 (not_10_out, d_ff_4_q);
  not not_11 (not_11_out, d_ff_1_q);
  not not_12 (not_12_out, d_ff_4_q);
  not not_13 (not_13_out, d_ff_1_q);
  not not_14 (not_14_out, d_ff_2_q);
  and and_7 (and_7_out, d_ff_1_q, and_3_out);
  and and_8 (and_8_out, not_3_out, d_ff_2_q, and_3_out);
  and and_9 (and_9_out, not_3_out, not_4_out, d_ff_3_q, and_3_out);
  and and_10 (and_10_out, not_3_out, not_4_out, not_5_out, d_ff_4_q, and_3_out);
  and and_11 (and_11_out, d_ff_2_q, and_4_out);
  and and_12 (and_12_out, not_6_out, d_ff_3_q, and_4_out);
  and and_13 (and_13_out, not_6_out, not_7_out, d_ff_4_q, and_4_out);
  and and_14 (and_14_out, not_6_out, not_7_out, not_8_out, d_ff_1_q, and_4_out);
  and and_15 (and_15_out, d_ff_3_q, and_5_out);
  and and_16 (and_16_out, not_9_out, d_ff_4_q, and_5_out);
  and and_17 (and_17_out, not_9_out, not_10_out, d_ff_1_q, and_5_out);
  and and_18 (and_18_out, not_9_out, not_10_out, not_11_out, d_ff_2_q, and_5_out);
  and and_19 (and_19_out, d_ff_4_q, and_6_out);
  and and_20 (and_20_out, not_12_out, d_ff_1_q, and_6_out);
  and and_21 (and_21_out, not_12_out, not_13_out, d_ff_2_q, and_6_out);
  and and_22 (and_22_out, not_12_out, not_13_out, not_14_out, d_ff_3_q, and_6_out);
  or or_5 (Grant_0, and_7_out, and_14_out, and_17_out, and_20_out);
  or or_6 (Grant_1, and_8_out, and_11_out, and_18_out, and_21_out);
  or or_7 (Grant_2, and_9_out, and_12_out, and_15_out, and_22_out);
  or or_8 (Grant_3, and_10_out, and_13_out, and_16_out, and_19_out);

  // Notes on the sheet:
  //   Clock
endmodule
